// Logisim project alu.circ as structural Verilog: 6 circuits, main circuit 8-bit Add
module _8_bit_Add (
  input  [7:0] in_1,
  input  [7:0] in_2,
  output [7:0] Sum,
  output Overflow
);

  wire n1_bit_add_1_carry_2, n1_bit_add_2_carry_2, n1_bit_add_3_carry_2, n1_bit_add_4_carry_2,
       n1_bit_add_5_carry_2, n1_bit_add_6_carry_2, n1_bit_add_7_carry_2;

  _1_bit_Add u_1_bit_add_1 (.Carry(1'b0), .A(in_1[0]), .B(in_2[0]), .Carry_2(n1_bit_add_1_carry_2), .Sum(Sum[0]));
  _1_bit_Add u_1_bit_add_2 (
    .Carry(n1_bit_add_1_carry_2), .A(in_2[1]), .B(in_1[1]), .Carry_2(n1_bit_add_2_carry_2), .Sum(Sum[1]));
  _1_bit_Add u_1_bit_add_3 (
    .Carry(n1_bit_add_2_carry_2), .A(in_2[2]), .B(in_1[2]), .Carry_2(n1_bit_add_3_carry_2), .Sum(Sum[2]));
  _1_bit_Add u_1_bit_add_4 (
    .Carry(n1_bit_add_3_carry_2), .A(in_1[3]), .B(in_2[3]), .Carry_2(n1_bit_add_4_carry_2), .Sum(Sum[3]));
  _1_bit_Add u_1_bit_add_5 (
    .Carry(n1_bit_add_4_carry_2), .A(in_1[4]), .B(in_2[4]), .Carry_2(n1_bit_add_5_carry_2), .Sum(Sum[4]));
  _1_bit_Add u_1_bit_add_6 (
    .Carry(n1_bit_add_5_carry_2), .A(in_1[5]), .B(in_2[5]), .Carry_2(n1_bit_add_6_carry_2), .Sum(Sum[5]));
  _1_bit_Add u_1_bit_add_7 (
    .Carry(n1_bit_add_6_carry_2), .A(in_1[6]), .B(in_2[6]), .Carry_2(n1_bit_add_7_carry_2), .Sum(Sum[6]));
  _1_bit_Add u_1_bit_add_8 (.Carry(n1_bit_add_7_carry_2), .A(in_1[7]), .B(in_2[7]), .Carry_2(Overflow), .Sum(Sum[7]));
endmodule

module XOR (
  input  in_1,
  input  in_2,
  input  in_3,
  output out_4
);

  wire and_1_out, xor_1_out;

  and and_1 (and_1_out, in_3, in_1, in_2);
  ExactlyOne xor_1 (.out(xor_1_out), .in1(in_1), .in3(in_3), .in4(in_2));
  or or_1 (out_4, xor_1_out, and_1_out);
endmodule

module _1_bit_Add (
  input  Carry,
  input  A,
  input  B,
  output Sum,
  output Carry_2
);

  wire and_1_out, and_2_out, and_3_out;

  and and_1 (and_1_out, Carry, A);
  and and_2 (and_2_out, A, B);
  or or_1 (Carry_2, and_1_out, and_2_out, and_3_out);
  and and_3 (and_3_out, B, Carry);
  XOR xor_1 (.in_1(A), .in_2(B), .in_3(Carry), .out_4(Sum));
endmodule

module _1_bit_Sub (
  input  A,
  input  B,
  input  Carry,
  output Carry_2,
  output A_B
);

  wire and_1_out, and_2_out, and_3_out, not_1_out, xor_1_out;

  not not_1 (not_1_out, A);
  and and_1 (and_1_out, Carry, not_1_out);
  and and_2 (and_2_out, not_1_out, B);
  or or_1 (Carry_2, and_1_out, and_2_out, and_3_out);
  and and_3 (and_3_out, Carry, B);
  xor xor_1 (xor_1_out, A, B);
  xor xor_2 (A_B, xor_1_out, Carry);
endmodule

module _8_bit_Sub (
  input  [7:0] A,
  input  [7:0] B,
  output Underflow,
  output [7:0] Difference
);

  wire n1_bit_sub_1_carry_2, n1_bit_sub_2_carry_2, n1_bit_sub_3_carry_2, n1_bit_sub_4_carry_2,
       n1_bit_sub_5_carry_2, n1_bit_sub_6_carry_2, n1_bit_sub_7_carry_2;

  _1_bit_Sub u_1_bit_sub_1 (.A(A[0]), .B(B[0]), .Carry(1'b0), .Carry_2(n1_bit_sub_1_carry_2), .A_B(Difference[0]));
  _1_bit_Sub u_1_bit_sub_2 (
    .A(A[1]), .B(B[1]), .Carry(n1_bit_sub_1_carry_2), .Carry_2(n1_bit_sub_2_carry_2), .A_B(Difference[1]));
  _1_bit_Sub u_1_bit_sub_3 (
    .A(A[2]), .B(B[2]), .Carry(n1_bit_sub_2_carry_2), .Carry_2(n1_bit_sub_3_carry_2), .A_B(Difference[2]));
  _1_bit_Sub u_1_bit_sub_4 (
    .A(A[3]), .B(B[3]), .Carry(n1_bit_sub_3_carry_2), .Carry_2(n1_bit_sub_4_carry_2), .A_B(Difference[3]));
  _1_bit_Sub u_1_bit_sub_5 (
    .A(A[4]), .B(B[4]), .Carry(n1_bit_sub_4_carry_2), .Carry_2(n1_bit_sub_5_carry_2), .A_B(Difference[4]));
  _1_bit_Sub u_1_bit_sub_6 (
    .A(A[5]), .B(B[5]), .Carry(n1_bit_sub_5_carry_2), .Carry_2(n1_bit_sub_6_carry_2), .A_B(Difference[5]));
  _1_bit_Sub u_1_bit_sub_7 (
    .A(A[6]), .B(B[6]), .Carry(n1_bit_sub_6_carry_2), .Carry_2(n1_bit_sub_7_carry_2), .A_B(Difference[6]));
  _1_bit_Sub u_1_bit_sub_8 (.A(A[7]), .B(B[7]), .Carry(n1_bit_sub_7_carry_2), .Carry_2(Underflow), .A_B(Difference[7]));
endmodule

module ALU (
  input  [7:0] A,
  input  [7:0] B,
  input  [1:0] Selector,
  output [7:0] out_4,
  output out_5
);

  wire n8_bit_add_1_overflow, n8_bit_sub_1_underflow;
  wire [7:0] and_1_out, n8_bit_add_1_sum, n8_bit_sub_1_difference, or_1_out;

  _8_bit_Add u_8_bit_add_1 (.in_1(B), .in_2(A), .Sum(n8_bit_add_1_sum), .Overflow(n8_bit_add_1_overflow));
  _8_bit_Sub u_8_bit_sub_1 (.A(A), .B(B), .Underflow(n8_bit_sub_1_underflow), .Difference(n8_bit_sub_1_difference));
  assign and_1_out = B & A;  // AND_Gate and_1, 8 bits wide
  assign or_1_out = B | A;  // OR_Gate or_1, 8 bits wide
  Multiplexer #(.select(2), .width(8)) multiplexer_1 (
    .in0(and_1_out), .in1(or_1_out), .in2(n8_bit_add_1_sum), .in3(n8_bit_sub_1_difference), .out(out_4),
    .sel(Selector));
  Multiplexer #(.select(2), .width(1)) multiplexer_2 (
    .in2(n8_bit_add_1_overflow), .in3(n8_bit_sub_1_underflow), .out(out_5), .sel(Selector));  // open: in0, in1
endmodule
