// Logisim project alb.circ as structural Verilog
module NAND (
  input  in_1,
  input  in_2,
  output out_3
);

  wire and_1_out;

  and and_1 (and_1_out, in_1, in_2);
  not not_1 (out_3, and_1_out);
endmodule

module NOR (
  input  in_1,
  input  in_2,
  output out_3
);

  wire or_1_out;

  or or_1 (or_1_out, in_1, in_2);
  not not_1 (out_3, or_1_out);
endmodule

module XOR (
  input  in_1,
  input  in_2,
  output out_3
);

  wire and_1_out, and_2_out, not_1_out, not_2_out;

  and and_1 (and_1_out, in_1, not_1_out);
  not not_1 (not_1_out, in_2);
  not not_2 (not_2_out, in_1);
  and and_2 (and_2_out, not_2_out, in_2);
  or or_1 (out_3, and_1_out, and_2_out);
endmodule

module _2_to_1MUX (
  input  S,
  input  A,
  input  B,
  output out_4
);

  wire and_1_out, and_2_out, not_1_out, not_2_out;

  not not_1 (not_1_out, S);
  not not_2 (not_2_out, not_1_out);
  and and_1 (and_1_out, not_2_out, A);
  and and_2 (and_2_out, not_1_out, B);
  or or_1 (out_4, and_1_out, and_2_out);
endmodule

module _4_to_1_MUX (
  input  A,
  input  B,
  input  S0,
  input  C,
  input  D,
  input  S1,
  output out_7
);

  wire n2_to_1mux_1_out_4, n2_to_1mux_2_out_4;

  _2_to_1MUX u_2_to_1mux_1 (.S(S0), .A(A), .B(B), .out_4(n2_to_1mux_1_out_4));
  _2_to_1MUX u_2_to_1mux_2 (.S(S0), .A(C), .B(D), .out_4(n2_to_1mux_2_out_4));
  _2_to_1MUX u_2_to_1mux_3 (.S(S1), .A(n2_to_1mux_1_out_4), .B(n2_to_1mux_2_out_4), .out_4(out_7));
endmodule
