// Logisim project next-state.circ as structural Verilog: 3 circuits, main circuit main
module main (
  input  NScar,
  input  EWcar,
  input  Reset,
  output out_4,
  output out_5
);

  wire clock_1_out;

  next_state next_state_1 (.NScar(NScar), .EWcar(EWcar), .CurrentState(out_4), .Reset(Reset), .out_5(out_5));
  Clock #(.highDuration(1), .lowDuration(1)) clock_1 (.out(clock_1_out));
  D_Flip_Flop d_ff_1 (.clk(clock_1_out), .D(out_5), .Q(out_4));  // open: Qn, preset, en, reset
endmodule

module next_state (
  input  NScar,
  input  EWcar,
  input  CurrentState,
  input  Reset,
  output out_5
);

  wire and_1_out, and_2_out, not_1_out, not_2_out, or_1_out;

  not not_1 (not_1_out, NScar);
  not not_2 (not_2_out, CurrentState);
  and and_1 (and_1_out, not_1_out, CurrentState);
  and and_2 (and_2_out, EWcar, not_2_out);
  or or_1 (or_1_out, and_1_out, and_2_out);
  or or_2 (out_5, or_1_out, Reset);

  // Notes on the sheet:
  //   NextState
endmodule

module Flip_Flop (
  input  d,
  output q
);

  wire clock_1_out;

  Clock #(.highDuration(1), .lowDuration(1)) clock_1 (.out(clock_1_out));
  and and_1 (q, clock_1_out, d);

  // Notes on the sheet:
  //   Clock
endmodule
