// Logisim project cpu.circ as structural Verilog: 11 circuits, main circuit CPU
module _8_bit_Add (
  input  [7:0] A,
  input  [7:0] B,
  output [7:0] Sum,
  output Overflow
);

  wire n1_bit_add_1_carry_2, n1_bit_add_2_carry_2, n1_bit_add_3_carry_2, n1_bit_add_4_carry_2,
       n1_bit_add_5_carry_2, n1_bit_add_6_carry_2, n1_bit_add_7_carry_2;

  _1_bit_Add u_1_bit_add_1 (.Carry(1'b0), .A(A[0]), .B(B[0]), .Carry_2(n1_bit_add_1_carry_2), .Sum(Sum[0]));
  _1_bit_Add u_1_bit_add_2 (
    .Carry(n1_bit_add_1_carry_2), .A(B[1]), .B(A[1]), .Carry_2(n1_bit_add_2_carry_2), .Sum(Sum[1]));
  _1_bit_Add u_1_bit_add_3 (
    .Carry(n1_bit_add_2_carry_2), .A(B[2]), .B(A[2]), .Carry_2(n1_bit_add_3_carry_2), .Sum(Sum[2]));
  _1_bit_Add u_1_bit_add_4 (
    .Carry(n1_bit_add_3_carry_2), .A(A[3]), .B(B[3]), .Carry_2(n1_bit_add_4_carry_2), .Sum(Sum[3]));
  _1_bit_Add u_1_bit_add_5 (
    .Carry(n1_bit_add_4_carry_2), .A(A[4]), .B(B[4]), .Carry_2(n1_bit_add_5_carry_2), .Sum(Sum[4]));
  _1_bit_Add u_1_bit_add_6 (
    .Carry(n1_bit_add_5_carry_2), .A(A[5]), .B(B[5]), .Carry_2(n1_bit_add_6_carry_2), .Sum(Sum[5]));
  _1_bit_Add u_1_bit_add_7 (
    .Carry(n1_bit_add_6_carry_2), .A(A[6]), .B(B[6]), .Carry_2(n1_bit_add_7_carry_2), .Sum(Sum[6]));
  _1_bit_Add u_1_bit_add_8 (.Carry(n1_bit_add_7_carry_2), .A(A[7]), .B(B[7]), .Carry_2(Overflow), .Sum(Sum[7]));
endmodule

module XOR (
  input  in_1,
  input  in_2,
  input  in_3,
  output out_4
);

  wire and_1_out, xor_1_out;

  and and_1 (and_1_out, in_3, in_1, in_2);
  ExactlyOne xor_1 (.out(xor_1_out), .in1(in_1), .in3(in_3), .in4(in_2));
  or or_1 (out_4, xor_1_out, and_1_out);
endmodule

module _1_bit_Add (
  input  Carry,
  input  A,
  input  B,
  output Sum,
  output Carry_2
);

  wire and_1_out, and_2_out, and_3_out;

  and and_1 (and_1_out, Carry, A);
  and and_2 (and_2_out, A, B);
  or or_1 (Carry_2, and_1_out, and_2_out, and_3_out);
  and and_3 (and_3_out, B, Carry);
  XOR xor_1 (.in_1(A), .in_2(B), .in_3(Carry), .out_4(Sum));
endmodule

module _1_bit_Sub (
  input  A,
  input  B,
  input  Carry,
  output Carry_2,
  output A_B
);

  wire and_1_out, and_2_out, and_3_out, not_1_out, xor_1_out;

  not not_1 (not_1_out, A);
  and and_1 (and_1_out, Carry, not_1_out);
  and and_2 (and_2_out, not_1_out, B);
  or or_1 (Carry_2, and_1_out, and_2_out, and_3_out);
  and and_3 (and_3_out, Carry, B);
  xor xor_1 (xor_1_out, A, B);
  xor xor_2 (A_B, xor_1_out, Carry);
endmodule

module _8_bit_Sub (
  input  [7:0] A,
  input  [7:0] B,
  output Underflow,
  output [7:0] Difference
);

  wire n1_bit_sub_1_carry_2, n1_bit_sub_2_carry_2, n1_bit_sub_3_carry_2, n1_bit_sub_4_carry_2,
       n1_bit_sub_5_carry_2, n1_bit_sub_6_carry_2, n1_bit_sub_7_carry_2;

  _1_bit_Sub u_1_bit_sub_1 (.A(A[0]), .B(B[0]), .Carry(1'b0), .Carry_2(n1_bit_sub_1_carry_2), .A_B(Difference[0]));
  _1_bit_Sub u_1_bit_sub_2 (
    .A(A[1]), .B(B[1]), .Carry(n1_bit_sub_1_carry_2), .Carry_2(n1_bit_sub_2_carry_2), .A_B(Difference[1]));
  _1_bit_Sub u_1_bit_sub_3 (
    .A(A[2]), .B(B[2]), .Carry(n1_bit_sub_2_carry_2), .Carry_2(n1_bit_sub_3_carry_2), .A_B(Difference[2]));
  _1_bit_Sub u_1_bit_sub_4 (
    .A(A[3]), .B(B[3]), .Carry(n1_bit_sub_3_carry_2), .Carry_2(n1_bit_sub_4_carry_2), .A_B(Difference[3]));
  _1_bit_Sub u_1_bit_sub_5 (
    .A(A[4]), .B(B[4]), .Carry(n1_bit_sub_4_carry_2), .Carry_2(n1_bit_sub_5_carry_2), .A_B(Difference[4]));
  _1_bit_Sub u_1_bit_sub_6 (
    .A(A[5]), .B(B[5]), .Carry(n1_bit_sub_5_carry_2), .Carry_2(n1_bit_sub_6_carry_2), .A_B(Difference[5]));
  _1_bit_Sub u_1_bit_sub_7 (
    .A(A[6]), .B(B[6]), .Carry(n1_bit_sub_6_carry_2), .Carry_2(n1_bit_sub_7_carry_2), .A_B(Difference[6]));
  _1_bit_Sub u_1_bit_sub_8 (.A(A[7]), .B(B[7]), .Carry(n1_bit_sub_7_carry_2), .Carry_2(Underflow), .A_B(Difference[7]));
endmodule

module ALU (
  input  [7:0] A,
  input  [7:0] B,
  input  [1:0] ALUctr,
  output [7:0] Output,
  output Overflow
);

  wire n8_bit_add_1_overflow, n8_bit_sub_1_underflow;
  wire [7:0] and_1_out, n8_bit_add_1_sum, n8_bit_sub_1_difference, or_1_out;

  _8_bit_Add u_8_bit_add_1 (.A(A), .B(B), .Sum(n8_bit_add_1_sum), .Overflow(n8_bit_add_1_overflow));
  _8_bit_Sub u_8_bit_sub_1 (.A(A), .B(B), .Underflow(n8_bit_sub_1_underflow), .Difference(n8_bit_sub_1_difference));
  assign or_1_out = B | A;  // OR_Gate or_1, 8 bits wide
  assign and_1_out = A & B;  // AND_Gate and_1, 8 bits wide
  Multiplexer #(.select(2), .width(8)) multiplexer_1 (
    .in0(or_1_out), .in1(n8_bit_add_1_sum), .in2(and_1_out), .in3(n8_bit_sub_1_difference), .out(Output),
    .sel(ALUctr));
  Multiplexer #(.select(2), .width(1)) multiplexer_2 (
    .in2(n8_bit_add_1_overflow), .in3(n8_bit_sub_1_underflow), .out(Overflow), .sel(ALUctr));  // open: in0, in1
endmodule

module RegFile (
  input  rd,
  input  rs1,
  input  rs2,
  input  RegWrite,
  input  [7:0] Bus_W,
  input  clk,
  input  [7:0] Bus_temp,
  input  Clear,
  output [7:0] Bus_A,
  output [7:0] Bus_B,
  output [7:0] R0_R1
);

  wire and_1_out, and_2_out, not_1_out;
  wire [7:0] multiplexer_1_out, multiplexer_2_out, multiplexer_5_out, register_1_q, register_2_q;

  not not_1 (not_1_out, rd);
  and and_1 (and_1_out, RegWrite, not_1_out);
  and and_2 (and_2_out, rd, RegWrite);
  Multiplexer #(.select(1), .width(8)) multiplexer_1 (
    .in0(Bus_W), .in1(register_1_q), .out(multiplexer_1_out), .sel(and_1_out));
  Multiplexer #(.select(1), .width(8)) multiplexer_2 (
    .in0(Bus_W), .in1(register_2_q), .out(multiplexer_2_out), .sel(and_2_out));
  Register #(.width(8)) register_1 (.D(multiplexer_1_out), .Q(register_1_q), .clk(clk), .clr(Clear));  // open: en
  Register #(.width(8)) register_2 (.D(multiplexer_2_out), .Q(register_2_q), .clk(clk), .clr(Clear));  // open: en
  Multiplexer #(.select(1), .width(8)) multiplexer_3 (.in0(register_1_q), .in1(register_2_q), .out(Bus_A), .sel(rs1));
  Multiplexer #(.select(1), .width(8)) multiplexer_4 (.in0(register_1_q), .in1(register_2_q), .out(Bus_B), .sel(rs2));
  Multiplexer #(.select(1), .width(8)) multiplexer_5 (
    .in0(register_1_q), .in1(register_2_q), .out(multiplexer_5_out), .sel(rd));
  _8_bit_Sub u_8_bit_sub_1 (.A(register_1_q), .B(register_2_q), .Difference(R0_R1));  // open: Underflow

  // Notes on the sheet:
  //   R0
  //   R1
  //   R0-R1
endmodule

module CPU (
  output [7:0] Fetch
);

  wire clock_1_out, control_1_alusrc, control_1_lui, control_1_memtoreg, control_1_memwr, control_1_ori,
       control_1_regwr, not_1_out;
  wire [1:0] control_1_aluctr, control_1_npc;
  wire [7:0] alu_1_output, multiplexer_1_out, multiplexer_2_out, multiplexer_3_out, multiplexer_4_out,
       ram_1_data, regfile_1_bus_a, regfile_1_bus_b, regfile_1_r0_r1, undriven, zeroext_1_output;

  Clock #(.highDuration(1), .lowDuration(1)) clock_1 (.out(clock_1_out));
  RegFile regfile_1 (
    .RegWrite(control_1_regwr), .Bus_W(multiplexer_4_out), .clk(clock_1_out), .Bus_temp(undriven),
    .rd(Fetch[4]), .rs1(Fetch[3]), .rs2(Fetch[2]), .Bus_A(regfile_1_bus_a), .Bus_B(regfile_1_bus_b),
    .R0_R1(regfile_1_r0_r1));  // open: Clear
  zeroExt zeroext_1 (.immed(Fetch), .\output (zeroext_1_output));
  Multiplexer #(.select(1), .width(8)) multiplexer_1 (
    .in0(regfile_1_bus_a), .in1(undriven), .out(multiplexer_1_out), .sel(control_1_ori));
  Multiplexer #(.select(1), .width(8)) multiplexer_2 (
    .in0(regfile_1_bus_b), .in1(zeroext_1_output), .out(multiplexer_2_out), .sel(control_1_alusrc));
  Control control_1 (
    .instruction(Fetch), .RegWr(control_1_regwr), .nPC(control_1_npc), .MemWr(control_1_memwr),
    .MemtoReg(control_1_memtoreg), .ALUSrc(control_1_alusrc), .ALUctr(control_1_aluctr), .lui(control_1_lui),
    .ori(control_1_ori));
  Fetch fetch_1 (.clk(clock_1_out), .R0_R1(regfile_1_r0_r1), .nPC(control_1_npc), .Output(Fetch));
  ALU alu_1 (
    .A(multiplexer_1_out), .B(multiplexer_2_out), .ALUctr(control_1_aluctr), .Output(alu_1_output));  // open: Overflow
  not not_1 (not_1_out, control_1_memwr);
  Multiplexer #(.select(1), .width(8)) multiplexer_3 (
    .in0(alu_1_output), .in1(ram_1_data), .out(multiplexer_3_out), .sel(control_1_memtoreg));
  RAM #(.addrWidth(4), .dataWidth(8)) ram_1 (
    .addr(Fetch[3:0]), .data(ram_1_data), .sel(1'b1), .clk(clock_1_out), .ld(not_1_out));  // open: clr
  Multiplexer #(.select(1), .width(8)) multiplexer_4 (
    .in0(multiplexer_3_out), .in1({Fetch[0], Fetch[1], Fetch[2], Fetch[3], 4'b0000}),
    .out(multiplexer_4_out), .sel(control_1_lui));
  assign ram_1_data = control_1_memwr ? undriven : 8'bz;  // Controlled_Buffer controlled_buffer_1

  // Notes on the sheet:
  //   RegF
  //   zero
  //   ori
  //   ALU
  //   lui
endmodule

module Fetch (
  input  [1:0] nPC,
  input  clk,
  input  [7:0] R0_R1,
  output [7:0] Output
);

  wire or_1_out;
  wire [7:0] multiplexer_1_out, multiplexer_2_out, n8_bit_add_1_sum, register_1_q;

  Register #(.width(8)) register_1 (.D(multiplexer_2_out), .Q(register_1_q), .clk(clk));  // open: en, clr
  _8_bit_Add u_8_bit_add_1 (.A(register_1_q), .B(8'h1), .Sum(n8_bit_add_1_sum));  // open: Overflow
  // Probe on register_1_q[6]
  // Probe on register_1_q[7]
  // Probe on register_1_q[5]
  // Probe on register_1_q
  // Probe on register_1_q
  // Probe on Output[3]
  // Probe on Output[2]
  // Probe on Output[0]
  // Probe on Output[1]
  // Probe on Output
  // Probe on n8_bit_add_1_sum
  or or_1 (or_1_out, R0_R1[0], R0_R1[1], R0_R1[2], R0_R1[3], R0_R1[4], R0_R1[5], R0_R1[6], R0_R1[7]);
  // Probe on n8_bit_add_1_sum
  // Probe on register_1_q[5]
  // Probe on register_1_q[6]
  // Probe on register_1_q[7]
  // Probe on register_1_q[4]
  // Probe on register_1_q[4]
  // Probe on Output[3]
  // Probe on Output[2]
  // Probe on Output[1]
  // Probe on Output[0]
  Multiplexer #(.select(1), .width(8)) multiplexer_1 (
    .in0({register_1_q[7:4], Output[3:0]}), .in1(n8_bit_add_1_sum), .out(multiplexer_1_out), .sel(or_1_out));
  // Probe on {register_1_q[7:4], Output[3:0]}
  Multiplexer #(.select(2), .width(8)) multiplexer_2 (
    .in0(n8_bit_add_1_sum), .in1({register_1_q[7:4], Output[3:0]}), .in2(multiplexer_1_out),
    .in3(register_1_q), .out(multiplexer_2_out), .sel(nPC));
  RAM #(.addrWidth(8), .dataWidth(8)) ram_1 (
    .addr(register_1_q), .data(Output), .sel(1'b1), .ld(1'b1));  // open: clk, clr

  // Notes on the sheet:
  //   JEQ
  //   Add
  //   If r0-r1 =0 then pc=pc&imm
  //   nPC = 0 then pc+=1
  //   nPC = 1 jump
  //   nPC = 2 jeq
  //   nPC = 3 halt
endmodule

module zeroExt (
  input  [7:0] immed,
  output [7:0] \output 
);


  assign \output  = {4'b0000, immed[3:0]};
endmodule

module Control (
  input  [7:0] instruction,
  output RegWr,
  output [1:0] nPC,
  output MemWr,
  output MemtoReg,
  output ALUSrc,
  output [1:0] ALUctr,
  output lui,
  output ori
);

  wire and_1_out, and_2_out, and_3_out, and_8_out, and_9_out, not_1_out, not_2_out, not_3_out, not_4_out,
       not_5_out, not_6_out, not_7_out, not_8_out, not_9_out, not_10_out, not_11_out, not_12_out, not_13_out;

  // Probe on instruction[5]
  // Probe on instruction[7]
  // Probe on instruction[6]
  not not_1 (not_1_out, instruction[7]);
  not not_2 (not_2_out, instruction[6]);
  not not_3 (not_3_out, instruction[6]);
  not not_4 (not_4_out, instruction[5]);
  not not_5 (not_5_out, instruction[7]);
  not not_6 (not_6_out, instruction[7]);
  not not_7 (not_7_out, instruction[7]);
  not not_8 (not_8_out, instruction[6]);
  not not_9 (not_9_out, instruction[7]);
  not not_10 (not_10_out, instruction[5]);
  not not_11 (not_11_out, instruction[7]);
  not not_12 (not_12_out, instruction[6]);
  not not_13 (not_13_out, instruction[5]);
  and and_1 (and_1_out, not_1_out, not_2_out);
  and and_2 (and_2_out, not_3_out, not_4_out);
  and and_3 (and_3_out, not_5_out, instruction[5]);
  and and_4 (nPC[1], instruction[7], instruction[5]);
  and and_5 (nPC[0], instruction[7], instruction[6]);
  and and_6 (MemWr, not_6_out, instruction[6]);
  and and_7 (MemtoReg, not_7_out, not_8_out, instruction[5]);
  and and_8 (and_8_out, not_9_out, instruction[5]);
  and and_9 (and_9_out, instruction[7], not_10_out);
  and and_10 (ori, instruction[7], not_12_out, not_13_out);
  or or_1 (RegWr, and_1_out, and_2_out, and_3_out);
  or or_2 (ALUSrc, and_8_out, and_9_out);
  and and_11 (lui, not_11_out, instruction[6], instruction[5]);
  // Probe on instruction[1:0]
  // Probe on nothing
  Multiplexer #(.select(3), .width(2)) multiplexer_1 (
    .in0(instruction[1:0]), .in4(2'b00), .out(ALUctr), .sel(instruction[7:5]));  // open: in1, in2, in3, in5, in6, in7

  // Notes on the sheet:
  //   2
  //   0
  //   1
endmodule
