// Logisim project example.circ as structural Verilog
module Read_Only_Mem (
  input  [7:0] Address,
  output [7:0] Output
);

  RAM #(.addrWidth(8)) ram_1 (.addr(Address), .data(Output), .sel(1'b1), .ld(1'b1));  // open: clk, clr

  // Notes on the sheet:
  //   This is how to set up the memory if you only want to read from it.  Reads are asynchronous so the clock is unnecssary.
endmodule

module Read_Write_Mem (
  input  [7:0] Input,
  input  [7:0] Address,
  input  Clock,
  input  Read_Write,
  output [7:0] Output
);

  wire not_1_out;

  not not_1 (not_1_out, Read_Write);
  RAM #(.addrWidth(8)) ram_1 (.addr(Address), .data(Output), .sel(1'b1), .clk(Clock), .ld(not_1_out));  // open: clr
  assign Output = Read_Write ? Input : 8'bz;  // Controlled_Buffer controlled_buffer_1

  // Notes on the sheet:
  //   This is how to set up the memory to both read and write.  If Read/Write is 0 then the output gets the 
  //   value of of memory at the address asynchronously.  If Read/Write is 1 then input is written to memory at address synchronously (when the clock next goes high)
endmodule
